# Fritzing sketch 3Blinker (saved by Fritzing 0.9.3b)
circuit board: 2.09986cm x 3.61666cm
breadboards: 1

parts:
  VCC1 = Battery block 9V
  R1 = Resistor [tolerance=±5% resistance=220 package=THT]
  LED2 = LED - 5mm [color="Red (633nm)" package="5 mm [THT]"]
  LED3 = LED - 5mm [color="Yellow (595nm)" package="5 mm [THT]"]
  LED4 = LED - 5mm [color="Green (565nm)" package="5 mm [THT]"]

nets (from the schematic view):
  N1: VCC1.-, LED4.cathode
  N2: VCC1.+, R1.Pin_0
  N3: R1.Pin_1, LED2.anode
  N4: LED2.cathode, LED3.anode
  N5: LED3.cathode, LED4.anode
