# Fritzing sketch AirQuality (saved by Fritzing 1.0.1rc)
circuit board: 10.9266cm x 10.9846cm

parts:
  DS1 = DS18B20 1-Wire Temperature Sensor [part_number=DS18B20]
  Arduino_Nano_R3 = Arduino Nano (Rev3.0)
  R1_4_7kΩ = Resistor [tolerance=±5% power=0.25 resistance=4.7k package=THT]
  Grove1_Display = Grove OLED 128x96
  Adafruit_PMSA003I = Adafruit PMSA003I Air Quality Breakout [part_number="Adafruit #4632"]
  microSD_Module_PG6SD = MicroSD Card Module
  Adafruit_HUZZAH_ESP8266 = Adafruit HUZZAH ESP8266 Breakout [part_number=2471]
  R1_1kΩ = Resistor [tolerance=±5% power=0.25 resistance=1k package=THT]

nets:
  GND: DS1.GND, Arduino_Nano_R3.GND, Grove1_Display.GND, Adafruit_PMSA003I.GND, microSD_Module_PG6SD.GND, Adafruit_HUZZAH_ESP8266.GND
  N1: DS1.DQ, Arduino_Nano_R3.D5
  N2: DS1.VDD, R1_4_7kΩ.Pin_1
  N3: Arduino_Nano_R3.D1/TX, R1_1kΩ.Pin_1
  N4: Arduino_Nano_R3.D0/RX, Adafruit_HUZZAH_ESP8266.TX
  N5: Arduino_Nano_R3.D10, microSD_Module_PG6SD.CS
  N6: Arduino_Nano_R3.D11/MOSI, microSD_Module_PG6SD.MOSI
  N7: Arduino_Nano_R3.D12/MISO, microSD_Module_PG6SD.MISO
  VCC: Arduino_Nano_R3.5V, R1_4_7kΩ.Pin_0, Grove1_Display.VCC, Adafruit_PMSA003I.VCC, microSD_Module_PG6SD.VCC, Adafruit_HUZZAH_ESP8266.V+
  N8: Arduino_Nano_R3.A5, Grove1_Display.SCL, Adafruit_PMSA003I.SCL
  N9: Arduino_Nano_R3.A4, Grove1_Display.SDA, Adafruit_PMSA003I.SDA
  N10: Arduino_Nano_R3.3V3, Adafruit_HUZZAH_ESP8266.EN
  N11: Arduino_Nano_R3.D13/SCK, microSD_Module_PG6SD.SCK
  N12: Adafruit_HUZZAH_ESP8266.RX, R1_1kΩ.Pin_0

custom parts:
  Adafruit PMSA003I Air Quality Breakout: Breathe easy, knowing that you can track and sense the quality of the air around you with this Adafruit PMSA003I Air Quality Breakout. This sensor is great for monitoring air quality, in a compact plug-in format. Best of all, unlike almost all other sensors we've seen that are UART interface, this one is I2C interface, which makes it a great match for single board Linux computers like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
