# Fritzing sketch Attiny85-audioPlayer (saved by Fritzing 0.9.3b)
circuit board: 5.0906cm x 3.23204cm
breadboards: 1

parts:
  IC1 = DIP - 8 pins [chip_label=Attiny85 package="DIP (Dual Inline) [THT]"]
  S1 = Pushbutton [package=THT]
  SP1 = SPEAKER [package=pcb_mount_speaker]
  VCC1 = Battery

nets:
  N1: IC1.(PCINT5/~RESET/ADC0/dW)_PB5, S1.leg1
  N2: IC1.(PCINT4/XTAL2/CLKO/OC1B/ADC2)_PB4, SP1.-
  GND: IC1.GND, S1.leg0, VCC1.-
  N3: IC1.PB1_(MISO/DO/AIN1/OC0B/OC1A/PCINT1), SP1.+
  N4: IC1.VCC, VCC1.+

notes:
  Attiny85
  audio board
  StanchevPCB
  2022

custom parts:
  DIP - 8 pins: A DIP stand-in part for whatever IC you want. With 8 pins on a 300mil dual inline package (DIP) footprint.
