# Fritzing sketch Attiny85-i2c (saved by Fritzing 0.9.3b)
circuit board: 2.4727cm x 3.02751cm
breadboards: 1

parts:
  U1 = attiny85 [package=dip]
  U2 = attiny85 [package=dip]
  R1 = Resistor [tolerance=±5% resistance=10k package=THT]
  R2 = Resistor [tolerance=±5% resistance=10k package=THT]

nets:
  GND: U1.Pin_4, U2.Pin_4
  N1: U1.Pin_6, U2.Pin_5, R1.Pin_1
  N2: U1.Pin_7, U2.Pin_7, R2.Pin_1
  5V: U1.Pin_8, U2.Pin_8, R1.Pin_0, R2.Pin_0
