# Fritzing sketch Attiny85game (saved by Fritzing 0.9.3b)
circuit board: 5.84957cm x 5.54794cm
breadboards: 1

parts:
  U1 = attiny85 [package=dip]
  RELAY1 = CAR RELAY [part_number=NVF4-2 package=THT]
  LED1 = LED - 5mm [color="Red (633nm)" package="5 mm [THT]"]
  Grove1 = Grove OLED 128x96
  R1 = Resistor [tolerance=±5% resistance=6.8k package=THT]
  R2 = Resistor [tolerance=±5% resistance=1k package=THT]
  SG1 = Buzzer 12mm [package=buzzer-ccv-kit]
  S2 = Pushbutton [package="[THT]"]
  R3 = Resistor [tolerance=±5% resistance=10k package=THT]
  R4 = Resistor [tolerance=±5% resistance=10k package=THT]
  S3 = Pushbutton [package="[THT]"]
  BAT1 = Battery Holders [package=battcon_245mm_pth]
  S1 = Pushbutton [package="[THT]"]

nets:
  N1: U1.Pin_1, S1.Pin_1, S1.Pin_2
  N2: U1.Pin_2, Grove1.SDA
  N3: U1.Pin_3, Grove1.SCL
  N4: U1.Pin_4, LED1.cathode, Grove1.GND, R1.Pin_0, SG1.2, R3.Pin_0, R4.Pin_0, BAT1.+
  N5: U1.Pin_5, S2.Pin_1, S2.Pin_2, R3.Pin_1
  N6: U1.Pin_6, SG1.1
  p7: U1.Pin_7, R4.Pin_1, S3.Pin_1, S3.Pin_2
  N7: U1.Pin_8, RELAY1.87A, LED1.anode, Grove1.VCC, R2.Pin_1, S2.Pin_3, S2.Pin_4, S3.Pin_3, S3.Pin_4
  N8: RELAY1.30, BAT1.-
  N9: R1.Pin_1, R2.Pin_0, S1.Pin_3, S1.Pin_4
