# Fritzing sketch Attiny85game (saved by Fritzing 0.9.3b)
circuit board: 5.38259cm x 8.21805cm
breadboards: 1

parts:
  LED1 = LED - 5mm [color="Red (633nm)" package="5 mm [THT]"]
  LED2 = LED - 5mm [color="Red (633nm)" package="5 mm [THT]"]
  LED3 = LED - 5mm [color="Red (633nm)" package="5 mm [THT]"]
  LED4 = LED - 5mm [color="Red (633nm)" package="5 mm [THT]"]
  LED5 = LED - 5mm [color="Red (633nm)" package="5 mm [THT]"]
  LED6 = LED - 5mm [color="Red (633nm)" package="5 mm [THT]"]
  LED7 = LED - 5mm [color="Red (633nm)" package="5 mm [THT]"]
  LED8 = LED - 5mm [color="Red (633nm)" package="5 mm [THT]"]
  LED9 = LED - 5mm [color="Red (633nm)" package="5 mm [THT]"]
  LED10 = LED - 5mm [color="Red (633nm)" package="5 mm [THT]"]
  LED11 = LED - 5mm [color="Red (633nm)" package="5 mm [THT]"]
  LED12 = LED - 5mm [color="Red (633nm)" package="5 mm [THT]"]
  LED13 = LED - 5mm [color="Red (633nm)" package="5 mm [THT]"]
  LED14 = LED - 5mm [color="Red (633nm)" package="5 mm [THT]"]
  LED15 = LED - 5mm [color="Red (633nm)" package="5 mm [THT]"]
  LED16 = LED - 5mm [color="Red (633nm)" package="5 mm [THT]"]
  LED17 = LED - 5mm [color="Red (633nm)" package="5 mm [THT]"]
  LED18 = LED - 5mm [color="Red (633nm)" package="5 mm [THT]"]
  LED19 = LED - 5mm [color="Red (633nm)" package="5 mm [THT]"]
  LED20 = LED - 5mm [color="Red (633nm)" package="5 mm [THT]"]
  R1 = Resistor [tolerance=±5% resistance=100 package=THT]
  R2 = Resistor [tolerance=±5% resistance=100 package=THT]
  R3 = Resistor [tolerance=±5% resistance=100 package=THT]
  R4 = Resistor [tolerance=±5% resistance=100 package=THT]
  R5 = Resistor [tolerance=±5% resistance=100 package=THT]
  IC1 = DIP - 8 pins [chip_label=Attiny85 package="DIP (Dual Inline) [THT]"]
  J2 = AVR ISP 6 Pin [package=2x3-ns]
  U1 = SWITCH_SPDT [package=kps-1290]
  VCC1 = Battery

nets:
  N1: LED1.cathode, LED2.cathode, LED3.cathode, LED4.cathode, LED8.anode, LED12.anode, LED16.anode, LED20.anode, R1.Pin_0
  N2: LED1.anode, LED5.cathode, LED5.anode, LED6.cathode, LED7.cathode, LED8.cathode, LED9.anode, LED13.anode, LED17.cathode, LED18.cathode, LED19.cathode, LED20.cathode, R2.Pin_0, R5.Pin_0
  N3: LED2.anode, LED6.anode, LED10.anode, LED17.anode
  N4: LED3.anode, LED7.anode, LED14.anode, LED18.anode
  N5: LED4.anode, LED11.anode, LED15.anode, LED19.anode
  N6: LED9.cathode, LED10.cathode, LED11.cathode, LED12.cathode, R3.Pin_0
  N7: LED13.cathode, LED14.cathode, LED15.cathode, LED16.cathode, R4.Pin_0
  MOSI: R1.Pin_1, IC1.PB0_(MOSI/DI/SDA/AIN0/OC0A/~OC1A/AREF/PCINT0), J2.4
  MISO: R2.Pin_1, IC1.PB1_(MISO/DO/AIN1/OC0B/OC1A/PCINT1), J2.1
  SCK: R3.Pin_1, IC1.PB2_(SCK/USCK/SCL/ADC1/T0/INT0/PCINT2), J2.3
  PB3: R4.Pin_1, IC1.(PCINT3/XTAL1/CLKI/~OC1B/ADC3)_PB3
  PB4: R5.Pin_1, IC1.(PCINT4/XTAL2/CLKO/OC1B/ADC2)_PB4
  RST: IC1.(PCINT5/~RESET/ADC0/dW)_PB5, J2.5
  GND: IC1.GND, J2.6, VCC1.-
  3.3V/VCC: IC1.VCC, J2.2, U1.P
  N8: U1.S, VCC1.+

notes:
  Attiny85  matrix board
  StanchevPCB
  2022

custom parts:
  DIP - 8 pins: A DIP stand-in part for whatever IC you want. With 8 pins on a 300mil dual inline package (DIP) footprint.
