# Fritzing sketch ESP32-minimum (saved by Fritzing 0.9.3b)
circuit board: 3.37225cm x 4.44819cm
breadboards: 1

parts:
  U1 = ESP8266 WiFi Module [part_number=ESP8266]
  R4 = Resistor [tolerance=±5% resistance=10k package=THT]
  R5 = Resistor [tolerance=±5% resistance=10k package=THT]
  S1 = Pushbutton [package=THT]
  R1 = Resistor [tolerance=±5% resistance=10k package=THT]
  R2 = Resistor [tolerance=±5% resistance=10k package=THT]
  R3 = Resistor [tolerance=±5% resistance=10k package=THT]
  C1 = Electrolytic Capacitor [capacitance=100nF package="100 mil [THT, electrolytic]"]
  S2 = Pushbutton [package=THT]

nets:
  3.3V/PWR: U1.VCC, R4.Pin_1, R5.Pin_1, R2.Pin_0, R3.Pin_1, C1.+
  N1: U1.GPIO_0, R4.Pin_0, S1.leg0
  N2: U1.GPIO_2, R5.Pin_0
  N3: U1.CH_PD, U1.ADC_0, R3.Pin_0
  GND: U1.GND, S1.leg1, R1.Pin_1, C1.-, S2.leg1
  N4: U1.GPIO_15, R1.Pin_0
  RST: U1.GPIO_16, U1.REST, R2.Pin_1, S2.leg0

notes:
  ESP32 MinBoard
  StanchevPCB
  2022
