# Fritzing sketch LampSwitch (saved by Fritzing 0.9.3b)
circuit board: 1.9121cm x 2.94355cm
breadboards: 1

parts:
  VCC1 = Battery block 9V
  S1 = Pushbutton [package="[SMD]"]
  LED1 = LED - 3mm [color="Green (560nm)" package="3 mm [THT]"]
  R1 = Resistor [tolerance=±5% resistance=470 package=THT]

nets:
  N1: VCC1.-, LED1.cathode
  N2: VCC1.+, S1.Pin_3, S1.Pin_4
  N3: S1.Pin_1, S1.Pin_2, LED1.anode, R1.Pin_0, R1.Pin_1

notes:
  LampSwitch
  StanchevPCB
  2022
