# Fritzing sketch PIC16F877A-Motor (saved by Fritzing 0.9.3b)
circuit board: 2.56612cm x 8.43079cm
breadboards: 1

parts:
  PIC_16F877A1 = PIC 16F877A [package=THT]
  L293D = L293D [package=THT]
  M1 = DC Motor
  S1 = Pushbutton [package=THT]

nets:
  N1: PIC_16F877A1.VSS#11, S1.leg1
  N2: PIC_16F877A1.RB0/INT, L293D.In_1
  N3: PIC_16F877A1.RB1, L293D.In_2
  N4: PIC_16F877A1.RB2, S1.leg0
  5V: L293D.Enable_1
  N5: L293D.Out_1_(_Controlled_by_Enable_1_), M1.pin_2
  GND: L293D.0V
  N6: L293D.Out_2_(_Controlled_by_Enable_1_), M1.pin_1

notes:
  PIC16f877A
  DC Motor Board
  StanchevPCB
  2022
