# Fritzing sketch PICBoard (saved by Fritzing 0.9.3b)
circuit board: 3.04821cm x 6.25251cm
breadboards: 1

parts:
  PIC_16F877A1 = PIC 16F877A [package=THT]
  R1 = Resistor [tolerance=±5% resistance=10k package=THT]
  LED1 = LED - 5mm [color="Red (633nm)" package="5 mm [THT]"]
  S1 = SWITCH-MOMENTARY-2 [package=tactile-switch-1101ne]

nets:
  N1: PIC_16F877A1.RD0/PSP0, R1.Pin_1, S1.1
  N2: PIC_16F877A1.RB0/INT, LED1.anode
  3.3V: R1.Pin_0
  GND: LED1.cathode, S1.2

notes:
  StanchevPCB
  2022
  PIC 16F877A1 Board
