# Fritzing sketch Attiny85-traffic (saved by Fritzing 0.9.3b)
circuit board: 2.51261cm x 7.90167cm
breadboards: 1

parts:
  Attiny85 = IC, DIP package, 8 pins [chip_label=Attiny85]
  U1 = Voltage Regulator - 5V [package="TO220 [THT]"]
  VCC1 = Battery block 9V
  S1 = Pushbutton [package=THT]
  S2 = Pushbutton [package=THT]
  R1 = Resistor [tolerance=±5% resistance=10k package=THT]
  LED1 = LED - 5mm [color="Red (633nm)" package="5 mm [THT]"]
  LED2 = LED - 5mm [color="Yellow (595nm)" package="5 mm [THT]"]
  LED3 = LED - 5mm [color="Green (565nm)" package="5 mm [THT]"]
  R2 = Resistor [tolerance=±5% resistance=100 package=THT]
  R3 = Resistor [tolerance=±5% resistance=100 package=THT]
  R4 = Resistor [tolerance=±5% resistance=100 package=THT]

nets:
  N1: Attiny85.pin3, LED3.anode
  N2: Attiny85.pin4, U1.GND, VCC1.-, R1.Pin_1, R2.Pin_1, R3.Pin_1, R4.Pin_1
  N3: Attiny85.pin5, LED1.anode
  N4: Attiny85.pin6, LED2.anode
  N5: Attiny85.pin7, S2.leg1, R1.Pin_0
  N6: Attiny85.pin8, S1.leg1, S2.leg0
  N7: U1.input_voltage, VCC1.+
  N8: U1.output_voltage, S1.leg0
  N9: LED1.cathode, R3.Pin_0
  N10: LED2.cathode, R2.Pin_0
  N11: LED3.cathode, R4.Pin_0

notes:
  StanchevPCB
  2022
  RGBLight Board
