# Fritzing sketch timer-555 (saved by Fritzing 0.9.3b)
circuit board: 4.64444cm x 4.94948cm
breadboards: 1

parts:
  U1 = 555 Timer [package="DIP8 [THT]"]
  R1 = Resistor [tolerance=±5% resistance=2.2M package=THT]
  R2 = Resistor [tolerance=±5% resistance=100k package=THT]
  C1 = Electrolytic Capacitor [capacitance=1µF package="100 mil [THT, electrolytic]"]
  C2 = Electrolytic Capacitor [capacitance=0.1µF package="100 mil [THT, electrolytic]"]
  R3 = Resistor [tolerance=±5% resistance=220 package=THT]
  S1 = Pushbutton [package="[THT]"]
  U2 = Voltage Regulator - 5V [package="TO220 [THT]"]
  C3 = Electrolytic Capacitor [capacitance=0.33µF package="100 mil [THT, electrolytic]"]
  C4 = Electrolytic Capacitor [capacitance=0.1µF package="100 mil [THT, electrolytic]"]
  VCC1 = Battery
  LED1 = LED - 5mm [color="Yellow (585nm)" package="5 mm [THT]"]

nets:
  GND: U1.Pin_1, C1.-, C2.-, U2.GND, C3.-, C4.-, VCC1.-
  N1: U1.Pin_2, U1.Pin_6, C1.+, S1.Pin_3, S1.Pin_4
  N2: U1.Pin_3, R3.Pin_0
  5V: U1.Pin_4, U1.Pin_8, R1.Pin_1, U2.output_voltage, C4.+, LED1.anode
  N3: U1.Pin_5, C2.+
  N4: U1.Pin_7, R1.Pin_0, R2.Pin_1
  N5: R2.Pin_0, S1.Pin_1, S1.Pin_2
  N6: R3.Pin_1, LED1.cathode
  N7: U2.input_voltage, C3.+, VCC1.+

notes:
  Timer555 Board
  StanchevPCB
  2022
